# Fritzing sketch Lab 1 (saved by Fritzing 0.9.4)
breadboards: 1

parts:
  U1 = 7400 4 x 2 Input NAND Gate [part_number=7400 package="DIP (Dual Inline) [THT]"]
  SW1 = DIP Switch 8 Position [package=dipswitch-08]
  R1 = Resistor [tolerance=±5% resistance=220 package=THT]
  R2 = Resistor [tolerance=±5% resistance=220 package=THT]
  R3 = Resistor [tolerance=±5% resistance=220 package=THT]
  U2 = 7400 4 x 2 Input NAND Gate [part_number=7400 package="DIP (Dual Inline) [THT]"]

nets:
  N1: U1.A1, SW1.8, R2.Pin_0, U2.Q2
  N2: U1.B1, SW1.7, R1.Pin_0
  N3: U1.Q1, U1.B4
  N4: U1.Q2, U1.A2
  N5: U1.B2, U1.B3
  GND: U1.GND, R1.Pin_1, R2.Pin_1, R3.Pin_1, U2.GND
  N6: U1.A3, U1.A4
  N7: U1.Q3, SW1.6, R3.Pin_0, U2.A2
  N8: U1.Q4, U2.A1, U2.B1
  5V: U1.VDD, SW1.9, SW1.10, SW1.11, U2.VDD
  N9: U2.Q1, U2.B4
  N10: U2.B2, U2.A4

notes:
  a
  b
  c
