# Fritzing sketch Lab 2 (saved by Fritzing 0.9.4)
circuit board: 8.46667cm x 5.64444cm
breadboards: 2

parts:
  U1 = 74153 Dual 4:1 MUX [part_number=74153 package="DIP16 [THT]"]
  U2 = 7474 Dual Positive Edge Triggered D Flip Flop [part_number=7474 package="DIP (Dual Inline) [THT]"]
  U4 = 7474 Dual Positive Edge Triggered D Flip Flop [part_number=7474 package="DIP (Dual Inline) [THT]"]
  U5 = 7400 4 x 2 Input NAND Gate [part_number=7400 package="DIP (Dual Inline) [THT]"]
  U6 = 7400 4 x 2 Input NAND Gate [part_number=7400 package="DIP (Dual Inline) [THT]"]
  U7 = 7404 Hex Inverter [part_number=7404 package=dil14]
  U8 = 7410 3 x 3 Input NAND Gate [part_number=7410 package="DIP (Dual Inline) [THT]"]
  SW1 = DIP Switch 8 Position [package=dipswitch-08]
  R2 = Resistor [tolerance=±5% resistance=220 package="1206 [SMD]"]
  R3 = Resistor [tolerance=±5% resistance=220 package="1206 [SMD]"]
  R4 = Resistor [tolerance=±5% resistance=220 package="1206 [SMD]"]
  R6 = Resistor [tolerance=±5% resistance=220 package="1206 [SMD]"]
  R7 = Resistor [tolerance=±5% resistance=220 package="1206 [SMD]"]
  R8 = Resistor [tolerance=±5% resistance=220 package="1206 [SMD]"]
  R9 = Resistor [tolerance=±5% resistance=220 package="1206 [SMD]"]
  R10 = Resistor [tolerance=±5% resistance=220 package="1206 [SMD]"]
  U9 = 74151 8:1 MUX [part_number=74151 package="DIP16 [THT]"]
  U12 = 7400 4 x 2 Input NAND Gate [part_number=7400 package="DIP (Dual Inline) [THT]"]
  U13 = 7404 Hex Inverter [part_number=7404 package=dil14]
  U14 = 7402 4 x 2 Input NOR Gate [part_number=7402 package="DIP (Dual Inline) [THT]"]
  U15 = 7400 4 x 2 Input NAND Gate [part_number=7400 package="DIP (Dual Inline) [THT]"]
  U16 = 74194 4 Bit Bi-Directional Shift Register [part_number=74194 package="DIP16 [THT]"]
  SW3 = DIP Switch 8 Position [package=dipswitch-08]
  U17 = 74194 4 Bit Bi-Directional Shift Register [part_number=74194 package="DIP16 [THT]"]
  R11 = Resistor [tolerance=±5% resistance=220 package="1206 [SMD]"]
  R12 = Resistor [tolerance=±5% resistance=220 package="1206 [SMD]"]
  R13 = Resistor [tolerance=±5% resistance=220 package="1206 [SMD]"]
  R14 = Resistor [tolerance=±5% resistance=220 package="1206 [SMD]"]
  R15 = Resistor [tolerance=±5% resistance=220 package="1206 [SMD]"]
  R16 = Resistor [tolerance=±5% resistance=220 package="1206 [SMD]"]
  U18 = 7402 4 x 2 Input NOR Gate [part_number=7402 package="DIP (Dual Inline) [THT]"]

nets:
  N1: U1.D0, U1.C1, U1.A1, U12.B1, U12.A2, U14.B1, U14.A2, U15.B1, U15.B4, U16.12
  GND: U1.G1, U1.G0, U1.GND, U2.GND, U4.GND, U5.GND, U6.GND, U7.GND, U8.GND, R2.Pin_1, R3.Pin_1, R4.Pin_1, R6.Pin_1, R7.Pin_1, R8.Pin_1, R9.Pin_1, R10.Pin_1, U9.7, U9.GND, U9.12, U12.GND, U13.GND, U14.GND, U15.GND, U16.GND, U17.GND, R11.Pin_1, R12.Pin_1, R13.Pin_1, R14.Pin_1, R15.Pin_1, R16.Pin_1, U18.GND
  N2: U1.C0, U1.B1, U9.5
  N3: U1.Y1, U16.2
  N4: U1.Y0, U17.2
  N5: U1.S1, SW1.5, R6.Pin_0
  N6: U1.A0, U1.B0, U1.D1, U12.A1, U12.Q2, U14.Q1, U14.B2, U15.A1, U15.A2, U17.12
  N7: U1.S0, SW1.4, R7.Pin_0
  5V: U1.VCC, U2.Q2, U2.Q3, U2.VDD, U4.Q2, U4.VDD, U5.VDD, U6.VDD, U7.VCC, U8.VDD, SW1.9, SW1.10, SW1.11, SW1.12, SW1.13, SW1.14, SW1.15, SW1.16, U9.1, U9.VCC, U12.VDD, U13.VCC, U14.VDD, U15.VDD, U16.1, U16.VCC, SW3.9, SW3.10, SW3.11, SW3.12, SW3.13, SW3.14, U17.1, U17.VCC, U18.VDD
  N8: U2.B1, U8.B2
  N9: U2.A2, U7.1A
  N10: U2.B3, U5.Q3, U6.Q2, U7.2A
  N11: U2.A4, U5.Q4
  N12: U4.B1, U6.Q4
  N13: U4.A2, U5.A2, U7.3A
  N14: U5.A1, U6.A1, U7.4A, SW1.3, R10.Pin_0
  N15: U5.B1, U6.B1, U7.1Y
  N16: U5.Q1, U8.A1
  N17: U5.Q2, U7.2Y, U8.Q1, U8.B4
  N18: U5.B2, U5.B4
  N19: U5.A3, U5.A4
  N20: U5.B3, U7.3Y, U8.B1
  N21: U6.Q1, U6.B4
  N22: U6.A2, U8.Q2
  N23: U6.B2, U6.A4
  N24: U7.4Y, U8.A2
  N25: U8.A4, U18.Q1, U18.B2
  N26: SW1.1, R8.Pin_0, U16.10, U18.A2
  N27: SW1.2, R9.Pin_0, U17.10, U18.B1
  N28: SW1.6, R4.Pin_0, U9.11
  N29: SW1.7, R3.Pin_0, U9.10
  N30: SW1.8, R2.Pin_0, U9.9
  N31: U9.2, U13.3A, U15.A3
  N32: U9.3, U13.2Y
  N33: U9.4, U13.1Y
  N34: U9.13, U13.3Y
  N35: U9.14, U14.Q2
  N36: U9.15, U12.B2
  N37: U12.Q1, U13.1A
  N38: U13.2A, U14.A1
  N39: U13.4Y, U17.9
  N40: U13.4A, U18.A1
  N41: U13.5Y, U16.9
  N42: U13.5A, U18.Q2
  N43: U15.Q1, U15.Q2, U15.A4
  N44: U15.B2, U15.B3
  N45: U15.Q3, U15.Q4
  N46: U16.3, SW3.6, U17.3, R13.Pin_0
  N47: U16.4, SW3.5, U17.4, R14.Pin_0
  N48: U16.5, SW3.4, U17.5, R15.Pin_0
  N49: U16.6, SW3.3, U17.6, R16.Pin_0
  N50: SW3.7, R12.Pin_0
  N51: SW3.8, R11.Pin_0

notes:
  Register B
  Register A
  F2
  F1
  F0
  R0
  R1
  Enable
  LoadA
  LoadB
  D0
  D1
  D3
  D2

custom parts:
  74153 Dual 4:1 MUX: 74153 Dual 4:1 Multiplexor
  7404 Hex Inverter: 74XX04 Hex Inverter, Modified by Zuofu Cheng (Aug 2020)
  7410 3 x 3 Input NAND Gate: 7410 3 x 2 Input NAND Gate
  74151 8:1 MUX: 74151 8:1 Multiplexor
